// Logisim project Space Invaders.circ as structural Verilog: 9 circuits, main circuit Pantalla y botones
module Pantalla_y_botones (
  input  POWER
);

  wire B_out, DER_out, IZQ_out;
  wire [7:0] pm_placa_madre_1_out_6, pm_placa_madre_1_out_7, pm_placa_madre_1_out_8, pm_placa_madre_1_out_9,
       pm_placa_madre_1_out_10, pm_placa_madre_1_out_11, pm_placa_madre_1_out_12, pm_placa_madre_1_out_13,
       pm_placa_madre_1_out_14, pm_placa_madre_1_out_15, pm_placa_madre_1_out_16, pm_placa_madre_1_out_17,
       pm_placa_madre_1_out_18, pm_placa_madre_1_out_19, pm_placa_madre_1_out_20, pm_placa_madre_1_out_21;

  DotMatrix #(.matrixcols(16), .matrixrows(8)) dotmatrix_1 (
    .col0(pm_placa_madre_1_out_6), .col1(pm_placa_madre_1_out_7), .col2(pm_placa_madre_1_out_8),
    .col3(pm_placa_madre_1_out_9), .col4(pm_placa_madre_1_out_10), .col5(pm_placa_madre_1_out_11),
    .col6(pm_placa_madre_1_out_12), .col7(pm_placa_madre_1_out_13), .col8(pm_placa_madre_1_out_14),
    .col9(pm_placa_madre_1_out_15), .col10(pm_placa_madre_1_out_16), .col11(pm_placa_madre_1_out_17),
    .col12(pm_placa_madre_1_out_18), .col13(pm_placa_madre_1_out_19), .col14(pm_placa_madre_1_out_20),
    .col15(pm_placa_madre_1_out_21));
  PM___Placa_madre pm_placa_madre_1 (
    .BOTON_GATILLO(B_out), .BOTON_IZQ(IZQ_out), .BOTON_DER(DER_out), .out_6(pm_placa_madre_1_out_6),
    .out_7(pm_placa_madre_1_out_7), .out_8(pm_placa_madre_1_out_8), .out_9(pm_placa_madre_1_out_9),
    .out_10(pm_placa_madre_1_out_10), .out_11(pm_placa_madre_1_out_11), .out_12(pm_placa_madre_1_out_12),
    .out_13(pm_placa_madre_1_out_13), .out_14(pm_placa_madre_1_out_14), .out_15(pm_placa_madre_1_out_15),
    .out_16(pm_placa_madre_1_out_16), .out_17(pm_placa_madre_1_out_17), .out_18(pm_placa_madre_1_out_18),
    .out_19(pm_placa_madre_1_out_19), .out_20(pm_placa_madre_1_out_20), .out_21(pm_placa_madre_1_out_21),
    .POWER(POWER), .in_5(DER_out));
  Button DER (.out(DER_out));
  Button IZQ (.out(IZQ_out));
  Button B (.out(B_out));
endmodule

module PM___Placa_madre (
  input  POWER,
  input  BOTON_GATILLO,
  input  BOTON_IZQ,
  input  BOTON_DER,
  input  in_5,
  output [7:0] out_6,
  output [7:0] out_7,
  output [7:0] out_8,
  output [7:0] out_9,
  output [7:0] out_10,
  output [7:0] out_11,
  output [7:0] out_12,
  output [7:0] out_13,
  output [7:0] out_14,
  output [7:0] out_15,
  output [7:0] out_16,
  output [7:0] out_17,
  output [7:0] out_18,
  output [7:0] out_19,
  output [7:0] out_20,
  output [7:0] out_21
);

  wire controlled_buffer_1_out, controlled_buffer_2_out, controlled_buffer_3_out, nave_1_out_3;
  wire [0:0] cdn_chip_desplazamiento_nave_1__0, cdn_chip_desplazamiento_nave_1__0_16;
  wire [3:0] \cpn_chip_posición_nave_1_output ;
  wire [7:0] cdn_chip_desplazamiento_nave_1__0_2, cdn_chip_desplazamiento_nave_1__0_3,
       cdn_chip_desplazamiento_nave_1__0_4, cdn_chip_desplazamiento_nave_1__0_5,
       cdn_chip_desplazamiento_nave_1__0_6, cdn_chip_desplazamiento_nave_1__0_7,
       cdn_chip_desplazamiento_nave_1__0_8, cdn_chip_desplazamiento_nave_1__0_9,
       cdn_chip_desplazamiento_nave_1__0_10, cdn_chip_desplazamiento_nave_1__0_11,
       cdn_chip_desplazamiento_nave_1__0_12, cdn_chip_desplazamiento_nave_1__0_13,
       cdn_chip_desplazamiento_nave_1__0_14, cdn_chip_desplazamiento_nave_1__0_15;

  assign controlled_buffer_1_out = POWER ? BOTON_GATILLO : 1'bz;  // Controlled_Buffer controlled_buffer_1
  assign controlled_buffer_2_out = POWER ? BOTON_IZQ : 1'bz;  // Controlled_Buffer controlled_buffer_2
  assign controlled_buffer_3_out = POWER ? BOTON_DER : 1'bz;  // Controlled_Buffer controlled_buffer_3
  \CPN___Chip_posición_nave  \cpn_chip_posición_nave_1  (
    .IZQ(controlled_buffer_2_out), .DER(controlled_buffer_3_out), .OUTPUT(\cpn_chip_posición_nave_1_output ),
    .POWER(POWER));
  CDN___Chip_desplazamiento_nave cdn_chip_desplazamiento_nave_1 (
    ._0(cdn_chip_desplazamiento_nave_1__0[0]), ._1(cdn_chip_desplazamiento_nave_1__0_2[1]),
    ._0_2(cdn_chip_desplazamiento_nave_1__0_2[0]), ._1_2(cdn_chip_desplazamiento_nave_1__0_3[1]),
    ._0_3(cdn_chip_desplazamiento_nave_1__0_3[0]), ._1_3(cdn_chip_desplazamiento_nave_1__0_4[1]),
    ._0_4(cdn_chip_desplazamiento_nave_1__0_4[0]), ._1_4(cdn_chip_desplazamiento_nave_1__0_5[1]),
    ._0_5(cdn_chip_desplazamiento_nave_1__0_5[0]), ._1_5(cdn_chip_desplazamiento_nave_1__0_6[1]),
    ._0_6(cdn_chip_desplazamiento_nave_1__0_6[0]), ._1_6(cdn_chip_desplazamiento_nave_1__0_7[1]),
    ._0_7(cdn_chip_desplazamiento_nave_1__0_7[0]), ._1_7(cdn_chip_desplazamiento_nave_1__0_8[1]),
    ._0_8(cdn_chip_desplazamiento_nave_1__0_8[0]), ._1_8(cdn_chip_desplazamiento_nave_1__0_9[1]),
    ._0_9(cdn_chip_desplazamiento_nave_1__0_9[0]), ._1_9(cdn_chip_desplazamiento_nave_1__0_10[1]),
    ._0_10(cdn_chip_desplazamiento_nave_1__0_10[0]), ._1_10(cdn_chip_desplazamiento_nave_1__0_11[1]),
    ._0_11(cdn_chip_desplazamiento_nave_1__0_11[0]), ._1_11(cdn_chip_desplazamiento_nave_1__0_12[1]),
    ._0_12(cdn_chip_desplazamiento_nave_1__0_12[0]), ._1_12(cdn_chip_desplazamiento_nave_1__0_13[1]),
    ._0_13(cdn_chip_desplazamiento_nave_1__0_13[0]), ._1_13(cdn_chip_desplazamiento_nave_1__0_14[1]),
    ._0_14(cdn_chip_desplazamiento_nave_1__0_14[0]), ._1_14(cdn_chip_desplazamiento_nave_1__0_15[1]),
    ._0_15(cdn_chip_desplazamiento_nave_1__0_15[0]), ._0_16(cdn_chip_desplazamiento_nave_1__0_16[0]),
    .INPUT(\cpn_chip_posición_nave_1_output ));
  CCB___Chip_controlador_bala ccb_chip_controlador_bala_1 (
    .in_2(\cpn_chip_posición_nave_1_output ), .INPUT_GATILLO(controlled_buffer_1_out),
    .out_4(cdn_chip_desplazamiento_nave_1__0_2[2]), .out_5(cdn_chip_desplazamiento_nave_1__0_2[3]),
    .out_6(cdn_chip_desplazamiento_nave_1__0_2[4]), .out_7(cdn_chip_desplazamiento_nave_1__0_2[5]),
    .out_8(cdn_chip_desplazamiento_nave_1__0_2[6]), .out_9(cdn_chip_desplazamiento_nave_1__0_2[7]),
    .out_10(cdn_chip_desplazamiento_nave_1__0_3[2]), .out_11(cdn_chip_desplazamiento_nave_1__0_3[3]),
    .out_12(cdn_chip_desplazamiento_nave_1__0_3[4]), .out_13(cdn_chip_desplazamiento_nave_1__0_3[5]),
    .out_14(cdn_chip_desplazamiento_nave_1__0_3[6]), .out_15(cdn_chip_desplazamiento_nave_1__0_3[7]),
    .out_16(cdn_chip_desplazamiento_nave_1__0_4[2]), .out_17(cdn_chip_desplazamiento_nave_1__0_4[3]),
    .out_18(cdn_chip_desplazamiento_nave_1__0_4[4]), .out_19(cdn_chip_desplazamiento_nave_1__0_4[5]),
    .out_20(cdn_chip_desplazamiento_nave_1__0_4[6]), .out_21(cdn_chip_desplazamiento_nave_1__0_4[7]),
    .out_22(cdn_chip_desplazamiento_nave_1__0_5[2]), .out_23(cdn_chip_desplazamiento_nave_1__0_5[3]),
    .out_24(cdn_chip_desplazamiento_nave_1__0_5[4]), .out_25(cdn_chip_desplazamiento_nave_1__0_5[5]),
    .out_26(cdn_chip_desplazamiento_nave_1__0_5[6]), .out_27(cdn_chip_desplazamiento_nave_1__0_5[7]),
    .out_28(cdn_chip_desplazamiento_nave_1__0_6[2]), .out_29(cdn_chip_desplazamiento_nave_1__0_6[3]),
    .out_30(cdn_chip_desplazamiento_nave_1__0_6[4]), .out_31(cdn_chip_desplazamiento_nave_1__0_6[5]),
    .out_32(cdn_chip_desplazamiento_nave_1__0_6[6]), .out_33(cdn_chip_desplazamiento_nave_1__0_6[7]),
    .out_34(cdn_chip_desplazamiento_nave_1__0_7[2]), .out_35(cdn_chip_desplazamiento_nave_1__0_7[3]),
    .out_36(cdn_chip_desplazamiento_nave_1__0_7[4]), .out_37(cdn_chip_desplazamiento_nave_1__0_7[5]),
    .out_38(cdn_chip_desplazamiento_nave_1__0_7[6]), .out_39(cdn_chip_desplazamiento_nave_1__0_7[7]),
    .out_40(cdn_chip_desplazamiento_nave_1__0_8[2]), .out_41(cdn_chip_desplazamiento_nave_1__0_8[3]),
    .out_42(cdn_chip_desplazamiento_nave_1__0_8[4]), .out_43(cdn_chip_desplazamiento_nave_1__0_8[5]),
    .out_44(cdn_chip_desplazamiento_nave_1__0_8[6]), .out_45(cdn_chip_desplazamiento_nave_1__0_8[7]),
    .out_46(cdn_chip_desplazamiento_nave_1__0_9[2]), .out_47(cdn_chip_desplazamiento_nave_1__0_9[3]),
    .out_48(cdn_chip_desplazamiento_nave_1__0_9[4]), .out_49(cdn_chip_desplazamiento_nave_1__0_9[5]),
    .out_50(cdn_chip_desplazamiento_nave_1__0_9[6]), .out_51(cdn_chip_desplazamiento_nave_1__0_9[7]),
    .out_52(cdn_chip_desplazamiento_nave_1__0_10[2]), .out_53(cdn_chip_desplazamiento_nave_1__0_10[3]),
    .out_54(cdn_chip_desplazamiento_nave_1__0_10[4]), .out_55(cdn_chip_desplazamiento_nave_1__0_10[5]),
    .out_56(cdn_chip_desplazamiento_nave_1__0_10[6]), .out_57(cdn_chip_desplazamiento_nave_1__0_10[7]),
    .out_58(cdn_chip_desplazamiento_nave_1__0_11[2]), .out_59(cdn_chip_desplazamiento_nave_1__0_11[3]),
    .out_60(cdn_chip_desplazamiento_nave_1__0_11[4]), .out_61(cdn_chip_desplazamiento_nave_1__0_11[5]),
    .out_62(cdn_chip_desplazamiento_nave_1__0_11[6]), .out_63(cdn_chip_desplazamiento_nave_1__0_11[7]),
    .out_64(cdn_chip_desplazamiento_nave_1__0_12[2]), .out_65(cdn_chip_desplazamiento_nave_1__0_12[3]),
    .out_66(cdn_chip_desplazamiento_nave_1__0_12[4]), .out_67(cdn_chip_desplazamiento_nave_1__0_12[5]),
    .out_68(cdn_chip_desplazamiento_nave_1__0_12[6]), .out_69(cdn_chip_desplazamiento_nave_1__0_12[7]),
    .out_70(cdn_chip_desplazamiento_nave_1__0_13[2]), .out_71(cdn_chip_desplazamiento_nave_1__0_13[3]),
    .out_72(cdn_chip_desplazamiento_nave_1__0_13[4]), .out_73(cdn_chip_desplazamiento_nave_1__0_13[5]),
    .out_74(cdn_chip_desplazamiento_nave_1__0_13[6]), .out_75(cdn_chip_desplazamiento_nave_1__0_13[7]),
    .out_76(cdn_chip_desplazamiento_nave_1__0_14[2]), .out_77(cdn_chip_desplazamiento_nave_1__0_14[3]),
    .out_78(cdn_chip_desplazamiento_nave_1__0_14[4]), .out_79(cdn_chip_desplazamiento_nave_1__0_14[5]),
    .out_80(cdn_chip_desplazamiento_nave_1__0_14[6]), .out_81(cdn_chip_desplazamiento_nave_1__0_14[7]),
    .out_82(cdn_chip_desplazamiento_nave_1__0_15[2]), .out_83(cdn_chip_desplazamiento_nave_1__0_15[3]),
    .out_84(cdn_chip_desplazamiento_nave_1__0_15[4]), .out_85(cdn_chip_desplazamiento_nave_1__0_15[5]),
    .out_86(cdn_chip_desplazamiento_nave_1__0_15[6]), .out_87(cdn_chip_desplazamiento_nave_1__0_15[7]),
    .POWER(POWER));
  LEDSWITCH___Power_switch_pantalla_LED ledswitch_power_switch_pantalla_led_1 (
    .POWER(POWER), .in_2({{7{1'b0}}, cdn_chip_desplazamiento_nave_1__0[0]}),
    .in_3(cdn_chip_desplazamiento_nave_1__0_2), .in_4(cdn_chip_desplazamiento_nave_1__0_3),
    .in_5(cdn_chip_desplazamiento_nave_1__0_4), .in_6(cdn_chip_desplazamiento_nave_1__0_5),
    .in_7(cdn_chip_desplazamiento_nave_1__0_6), .in_8(cdn_chip_desplazamiento_nave_1__0_7),
    .in_9(cdn_chip_desplazamiento_nave_1__0_8), .in_10(cdn_chip_desplazamiento_nave_1__0_9),
    .in_11(cdn_chip_desplazamiento_nave_1__0_10), .in_12(cdn_chip_desplazamiento_nave_1__0_11),
    .in_13(cdn_chip_desplazamiento_nave_1__0_12), .in_14(cdn_chip_desplazamiento_nave_1__0_13),
    .in_15(cdn_chip_desplazamiento_nave_1__0_14), .out_18(out_6), .out_19(out_7), .out_20(out_8),
    .out_21(out_9), .out_22(out_10), .out_23(out_11), .out_24(out_12), .out_25(out_13), .out_26(out_14),
    .out_27(out_15), .out_28(out_16), .out_29(out_17), .out_30(out_18), .out_31(out_19),
    .in_16(cdn_chip_desplazamiento_nave_1__0_15),
    .in_17({{7{1'b0}}, cdn_chip_desplazamiento_nave_1__0_16[0]}), .out_32(out_20), .out_33(out_21));
  Nave nave_1 (.APAGAR(in_5), .POWER(POWER), .out_3(nave_1_out_3));

  // Notes on the sheet:
  //   SP0
  //   SP15
  //   PANTALLA LED 8x16
endmodule

module CCB___Chip_controlador_bala (
  input  POWER,
  input  [3:0] in_2,
  input  INPUT_GATILLO,
  output out_4,
  output out_5,
  output out_6,
  output out_7,
  output out_8,
  output out_9,
  output out_10,
  output out_11,
  output out_12,
  output out_13,
  output out_14,
  output out_15,
  output out_16,
  output out_17,
  output out_18,
  output out_19,
  output out_20,
  output out_21,
  output out_22,
  output out_23,
  output out_24,
  output out_25,
  output out_26,
  output out_27,
  output out_28,
  output out_29,
  output out_30,
  output out_31,
  output out_32,
  output out_33,
  output out_34,
  output out_35,
  output out_36,
  output out_37,
  output out_38,
  output out_39,
  output out_40,
  output out_41,
  output out_42,
  output out_43,
  output out_44,
  output out_45,
  output out_46,
  output out_47,
  output out_48,
  output out_49,
  output out_50,
  output out_51,
  output out_52,
  output out_53,
  output out_54,
  output out_55,
  output out_56,
  output out_57,
  output out_58,
  output out_59,
  output out_60,
  output out_61,
  output out_62,
  output out_63,
  output out_64,
  output out_65,
  output out_66,
  output out_67,
  output out_68,
  output out_69,
  output out_70,
  output out_71,
  output out_72,
  output out_73,
  output out_74,
  output out_75,
  output out_76,
  output out_77,
  output out_78,
  output out_79,
  output out_80,
  output out_81,
  output out_82,
  output out_83,
  output out_84,
  output out_85,
  output out_86,
  output out_87
);

  wire and_1_out, and_2_out, and_3_out, and_4_out, and_5_out, and_6_out, and_7_out, and_8_out, and_9_out,
       and_10_out, and_11_out, and_12_out, and_13_out, and_14_out, and_15_out, decoder_1_out1,
       decoder_1_out2, decoder_1_out3, decoder_1_out4, decoder_1_out5, decoder_1_out6, decoder_1_out7,
       decoder_1_out8, decoder_1_out9, decoder_1_out10, decoder_1_out11, decoder_1_out12, decoder_1_out13,
       decoder_1_out14, not_1_out, SP_0_out_9;

  Decoder #(.select(4)) decoder_1 (
    .out1(decoder_1_out1), .out2(decoder_1_out2), .out3(decoder_1_out3), .out4(decoder_1_out4),
    .out5(decoder_1_out5), .out6(decoder_1_out6), .out7(decoder_1_out7), .out8(decoder_1_out8),
    .out9(decoder_1_out9), .out10(decoder_1_out10), .out11(decoder_1_out11), .out12(decoder_1_out12),
    .out13(decoder_1_out13), .out14(decoder_1_out14), .sel(in_2));  // open: out0, out15, en
  and and_1 (and_1_out, INPUT_GATILLO, not_1_out);
  not not_1 (not_1_out, SP_0_out_9);
  and and_2 (and_2_out, decoder_1_out1, and_1_out);
  and and_3 (and_3_out, decoder_1_out2, and_1_out);
  and and_4 (and_4_out, decoder_1_out3, and_1_out);
  and and_5 (and_5_out, decoder_1_out4, and_1_out);
  and and_6 (and_6_out, decoder_1_out5, and_1_out);
  and and_7 (and_7_out, decoder_1_out6, and_1_out);
  and and_8 (and_8_out, decoder_1_out7, and_1_out);
  and and_9 (and_9_out, decoder_1_out8, and_1_out);
  and and_10 (and_10_out, decoder_1_out9, and_1_out);
  and and_11 (and_11_out, decoder_1_out10, and_1_out);
  and and_12 (and_12_out, decoder_1_out11, and_1_out);
  and and_13 (and_13_out, decoder_1_out12, and_1_out);
  and and_14 (and_14_out, decoder_1_out13, and_1_out);
  and and_15 (and_15_out, decoder_1_out14, and_1_out);
  CDB___Chip_desplazamiento_bala SP_0 (
    .ENTRADA_GATILLO(and_2_out), ._2(out_4), ._3(out_5), ._4(out_6), ._5(out_7), ._6(out_8), ._7(out_9),
    .out_9(SP_0_out_9), .POWER(POWER));
  CDB___Chip_desplazamiento_bala SP_1 (
    .ENTRADA_GATILLO(and_3_out), ._2(out_10), ._3(out_11), ._4(out_12), ._5(out_13), ._6(out_14),
    ._7(out_15), .out_9(SP_0_out_9), .POWER(POWER));
  CDB___Chip_desplazamiento_bala SP_2 (
    .ENTRADA_GATILLO(and_4_out), ._2(out_16), ._3(out_17), ._4(out_18), ._5(out_19), ._6(out_20),
    ._7(out_21), .out_9(SP_0_out_9), .POWER(POWER));
  CDB___Chip_desplazamiento_bala SP_3 (
    .ENTRADA_GATILLO(and_5_out), ._2(out_22), ._3(out_23), ._4(out_24), ._5(out_25), ._6(out_26),
    ._7(out_27), .out_9(SP_0_out_9), .POWER(POWER));
  CDB___Chip_desplazamiento_bala SP_4 (
    .ENTRADA_GATILLO(and_6_out), ._2(out_28), ._3(out_29), ._4(out_30), ._5(out_31), ._6(out_32),
    ._7(out_33), .out_9(SP_0_out_9), .POWER(POWER));
  CDB___Chip_desplazamiento_bala SP_5 (
    .ENTRADA_GATILLO(and_7_out), ._2(out_34), ._3(out_35), ._4(out_36), ._5(out_37), ._6(out_38),
    ._7(out_39), .out_9(SP_0_out_9), .POWER(POWER));
  CDB___Chip_desplazamiento_bala SP_6 (
    .ENTRADA_GATILLO(and_8_out), ._2(out_40), ._3(out_41), ._4(out_42), ._5(out_43), ._6(out_44),
    ._7(out_45), .out_9(SP_0_out_9), .POWER(POWER));
  CDB___Chip_desplazamiento_bala SP_7 (
    .ENTRADA_GATILLO(and_9_out), ._2(out_46), ._3(out_47), ._4(out_48), ._5(out_49), ._6(out_50),
    ._7(out_51), .out_9(SP_0_out_9), .POWER(POWER));
  CDB___Chip_desplazamiento_bala SP_8 (
    .ENTRADA_GATILLO(and_10_out), ._2(out_52), ._3(out_53), ._4(out_54), ._5(out_55), ._6(out_56),
    ._7(out_57), .out_9(SP_0_out_9), .POWER(POWER));
  CDB___Chip_desplazamiento_bala SP_9 (
    .ENTRADA_GATILLO(and_11_out), ._2(out_58), ._3(out_59), ._4(out_60), ._5(out_61), ._6(out_62),
    ._7(out_63), .out_9(SP_0_out_9), .POWER(POWER));
  CDB___Chip_desplazamiento_bala SP_10 (
    .ENTRADA_GATILLO(and_12_out), ._2(out_64), ._3(out_65), ._4(out_66), ._5(out_67), ._6(out_68),
    ._7(out_69), .out_9(SP_0_out_9), .POWER(POWER));
  CDB___Chip_desplazamiento_bala SP_11 (
    .ENTRADA_GATILLO(and_13_out), ._2(out_70), ._3(out_71), ._4(out_72), ._5(out_73), ._6(out_74),
    ._7(out_75), .out_9(SP_0_out_9), .POWER(POWER));
  CDB___Chip_desplazamiento_bala SP_12 (
    .ENTRADA_GATILLO(and_14_out), ._2(out_76), ._3(out_77), ._4(out_78), ._5(out_79), ._6(out_80),
    ._7(out_81), .out_9(SP_0_out_9), .POWER(POWER));
  CDB___Chip_desplazamiento_bala SP_13 (
    .ENTRADA_GATILLO(and_15_out), ._2(out_82), ._3(out_83), ._4(out_84), ._5(out_85), ._6(out_86),
    ._7(out_87), .out_9(SP_0_out_9), .POWER(POWER));

  // Notes on the sheet:
  //   INPUT POSICIÓN
  //   LA BALA PASA AL CHIP DCB SOLO SI LA NAVE ESTÁ EN ESA POSICION DE COLUMNA Y NO HAYA NINGÚN OTRO CHIP CDB ACTIVO. 
  //   ESTO ÚLTIMO QUIERE DECIR QUE HAY UNA BALA RECORRIENDO OTRO REGISTRO. ASÍ SE EVITA QUE SE PUEDA DISPARAR OTRA BALA MIENTRAS HAYA UNA ACTIVA
endmodule

module CDB___Chip_desplazamiento_bala (
  input  ENTRADA_GATILLO,
  input  POWER,
  output _2,
  output _3,
  output _4,
  output _5,
  output _6,
  output _7,
  output out_9
);

  wire and_1_out, and_2_out, clock_1_out, nor_1_out, not_1_out, or_1_out;

  Clock clock_1 (.out(clock_1_out));
  and and_1 (and_1_out, ENTRADA_GATILLO, nor_1_out);
  or or_1 (or_1_out, and_1_out, and_2_out);
  and and_2 (and_2_out, clock_1_out, ~nor_1_out);  // AND_Gate
  nor nor_1 (nor_1_out, _2, _3, _4, _5, _6, _7);
  not not_1 (not_1_out, POWER);
  Shift_Register #(.length(6)) shift_register_1 (
    .in(and_1_out), .clk(or_1_out), .clr(not_1_out), .q0(_2), .q1(_3), .q2(_4), .q3(_5), .q4(_6), .q5(_7));  // open: shift, out, load, d0, d1, d2, d3, d4, d5
  or or_2 (out_9, _7, _6, _5, _4, _3, _2);

  // Notes on the sheet:
  //   REGISTRO DE LA COLUMNA ACTUAL
  //   FILA 
  //   INDICADOR REGISTRO ACTIVO
  //   SALIDAS DE LED DE (FILA, COLUMNA  ACTUAL)
  //   VAN CONECTADAS A LAS PATAS DEL SPLITTER CORRESPONDIENTE
endmodule

module \CPN___Chip_posición_nave  (
  input  IZQ,
  input  POWER,
  input  DER,
  output [3:0] OUTPUT
);

  wire and_1_out, and_2_out, and_3_out, and_4_out, and_5_out, and_6_out, and_7_out, and_8_out, and_9_out,
       and_10_out, and_11_out, and_12_out, and_13_out, and_14_out, and_15_out, and_16_out, and_17_out,
       and_18_out, and_19_out, and_20_out, and_21_out, and_22_out, and_23_out, and_24_out, and_25_out,
       and_26_out, and_27_out, and_28_out, and_29_out, and_30_out, and_31_out, and_32_out, and_33_out,
       and_34_out, and_35_out, and_36_out, not_1_out, not_2_out, not_3_out, not_4_out, not_5_out, not_6_out,
       not_7_out, not_8_out, not_9_out, not_10_out, not_11_out, not_12_out, not_13_out, not_14_out,
       not_15_out, not_16_out, not_17_out, not_18_out, not_19_out, not_20_out, not_21_out, not_22_out,
       not_23_out, not_24_out, not_25_out, not_26_out, not_27_out, not_28_out, not_29_out, not_30_out,
       not_31_out, not_32_out, not_33_out, not_34_out, not_35_out, not_36_out, not_37_out, not_38_out,
       not_39_out, not_40_out, not_41_out, not_42_out, not_43_out, not_44_out, not_45_out, not_46_out,
       not_47_out, not_48_out, not_49_out, not_50_out, not_51_out, not_52_out, not_53_out, not_54_out,
       not_55_out, not_56_out, not_57_out, not_58_out, not_59_out, or_1_out, or_2_out, or_3_out, or_4_out,
       or_5_out;

  and and_1 (and_1_out, DER, DER);
  and and_2 (and_2_out, IZQ, IZQ);
  not not_1 (not_1_out, IZQ);
  not not_2 (not_2_out, IZQ);
  not not_3 (not_3_out, OUTPUT[2]);
  not not_4 (not_4_out, IZQ);
  not not_5 (not_5_out, OUTPUT[1]);
  not not_6 (not_6_out, IZQ);
  not not_7 (not_7_out, IZQ);
  not not_8 (not_8_out, DER);
  not not_9 (not_9_out, OUTPUT[1]);
  not not_10 (not_10_out, OUTPUT[0]);
  not not_11 (not_11_out, OUTPUT[2]);
  not not_12 (not_12_out, OUTPUT[1]);
  not not_13 (not_13_out, OUTPUT[0]);
  not not_14 (not_14_out, DER);
  not not_15 (not_15_out, IZQ);
  not not_16 (not_16_out, OUTPUT[1]);
  not not_17 (not_17_out, IZQ);
  not not_18 (not_18_out, OUTPUT[0]);
  not not_19 (not_19_out, IZQ);
  not not_20 (not_20_out, DER);
  not not_21 (not_21_out, OUTPUT[1]);
  not not_22 (not_22_out, OUTPUT[0]);
  not not_23 (not_23_out, DER);
  not not_24 (not_24_out, OUTPUT[1]);
  not not_25 (not_25_out, OUTPUT[0]);
  not not_26 (not_26_out, DER);
  not not_27 (not_27_out, IZQ);
  not not_28 (not_28_out, OUTPUT[3]);
  not not_29 (not_29_out, OUTPUT[2]);
  not not_30 (not_30_out, OUTPUT[1]);
  not not_31 (not_31_out, OUTPUT[0]);
  not not_32 (not_32_out, OUTPUT[3]);
  not not_33 (not_33_out, OUTPUT[2]);
  not not_34 (not_34_out, OUTPUT[1]);
  not not_35 (not_35_out, DER);
  not not_36 (not_36_out, OUTPUT[3]);
  not not_37 (not_37_out, OUTPUT[0]);
  not not_38 (not_38_out, IZQ);
  not not_39 (not_39_out, OUTPUT[2]);
  not not_40 (not_40_out, OUTPUT[0]);
  not not_41 (not_41_out, IZQ);
  not not_42 (not_42_out, OUTPUT[1]);
  not not_43 (not_43_out, OUTPUT[0]);
  not not_44 (not_44_out, IZQ);
  not not_45 (not_45_out, OUTPUT[0]);
  not not_46 (not_46_out, DER);
  not not_47 (not_47_out, OUTPUT[3]);
  not not_48 (not_48_out, IZQ);
  not not_49 (not_49_out, DER);
  not not_50 (not_50_out, OUTPUT[2]);
  not not_51 (not_51_out, IZQ);
  not not_52 (not_52_out, DER);
  not not_53 (not_53_out, OUTPUT[1]);
  not not_54 (not_54_out, IZQ);
  not not_55 (not_55_out, DER);
  not not_56 (not_56_out, OUTPUT[3]);
  not not_57 (not_57_out, OUTPUT[2]);
  not not_58 (not_58_out, OUTPUT[1]);
  or or_1 (or_1_out, and_1_out, and_2_out);
  and and_3 (and_3_out, OUTPUT[2], OUTPUT[1], OUTPUT[0], not_1_out, DER);
  and and_4 (and_4_out, OUTPUT[3], not_2_out);
  and and_5 (and_5_out, OUTPUT[3], DER);
  and and_6 (and_6_out, OUTPUT[3], OUTPUT[0]);
  and and_7 (and_7_out, OUTPUT[3], OUTPUT[1]);
  and and_8 (and_8_out, OUTPUT[3], OUTPUT[2]);
  and and_9 (and_9_out, not_3_out, OUTPUT[1], OUTPUT[0], not_4_out, DER);
  and and_10 (and_10_out, OUTPUT[2], not_5_out, not_6_out);
  and and_11 (and_11_out, OUTPUT[2], not_7_out, not_8_out);
  and and_12 (and_12_out, OUTPUT[2], not_9_out, DER);
  and and_13 (and_13_out, OUTPUT[2], OUTPUT[0], IZQ);
  and and_14 (and_14_out, OUTPUT[2], OUTPUT[1], not_10_out);
  and and_15 (and_15_out, OUTPUT[3], not_11_out, not_12_out, not_13_out, IZQ, not_14_out);
  and and_16 (and_16_out, OUTPUT[3], OUTPUT[2], not_15_out);
  and and_17 (and_17_out, not_16_out, OUTPUT[0], not_17_out, DER);
  and and_18 (and_18_out, OUTPUT[1], not_18_out, not_19_out);
  and and_19 (and_19_out, OUTPUT[1], IZQ, DER);
  and and_20 (and_20_out, OUTPUT[1], OUTPUT[0], not_20_out);
  and and_21 (and_21_out, OUTPUT[2], not_21_out, not_22_out, IZQ, not_23_out);
  and and_22 (and_22_out, OUTPUT[3], not_24_out, not_25_out, IZQ, not_26_out);
  and and_23 (and_23_out, OUTPUT[3], OUTPUT[2], OUTPUT[1], not_27_out);
  and and_24 (and_24_out, not_28_out, not_29_out, not_30_out, not_31_out);
  and and_25 (and_25_out, not_32_out, not_33_out, not_34_out, not_35_out);
  and and_26 (and_26_out, not_36_out, not_37_out, not_38_out, DER);
  and and_27 (and_27_out, not_39_out, not_40_out, not_41_out, DER);
  and and_28 (and_28_out, not_42_out, not_43_out, not_44_out, DER);
  and and_29 (and_29_out, not_45_out, IZQ, not_46_out);
  and and_30 (and_30_out, not_47_out, OUTPUT[0], not_48_out, not_49_out);
  and and_31 (and_31_out, not_50_out, OUTPUT[0], not_51_out, not_52_out);
  and and_32 (and_32_out, not_53_out, OUTPUT[0], not_54_out, not_55_out);
  and and_33 (and_33_out, not_56_out, OUTPUT[0], IZQ, DER);
  and and_34 (and_34_out, not_57_out, OUTPUT[0], IZQ, DER);
  and and_35 (and_35_out, not_58_out, OUTPUT[0], IZQ, DER);
  or or_2 (or_2_out, and_3_out, and_4_out, and_5_out, and_6_out, and_7_out, and_8_out);
  or or_3 (or_3_out, and_17_out, and_18_out, and_19_out, and_20_out, and_21_out, and_22_out, and_23_out);
  and and_36 (and_36_out, or_1_out, or_1_out);
  or or_4 (or_4_out, and_9_out, and_10_out, and_11_out, and_12_out, and_13_out, and_14_out, and_15_out, and_16_out);
  or or_5 (or_5_out, and_24_out, and_25_out, and_26_out, and_27_out, and_28_out, and_29_out, and_30_out, and_31_out, and_32_out, and_33_out, and_34_out, and_35_out);
  D_Flip_Flop DA (.clk(and_36_out), .D(or_2_out), .Q(OUTPUT[3]), .reset(not_59_out));  // open: Qn, preset, en
  not not_59 (not_59_out, POWER);
  D_Flip_Flop DB (.clk(and_36_out), .D(or_4_out), .Q(OUTPUT[2]), .reset(not_59_out));  // open: Qn, preset, en
  D_Flip_Flop DC (.clk(and_36_out), .D(or_3_out), .Q(OUTPUT[1]), .reset(not_59_out));  // open: Qn, preset, en
  D_Flip_Flop DD (.clk(and_36_out), .D(or_5_out), .Q(OUTPUT[0]), .reset(not_59_out));  // open: Qn, preset, en

  // Notes on the sheet:
  //   INPUTS
  //   IMPLEMENTA EL MOVIMIENTO DEL PIXEL DE LA NAVE, TOMANDO COMO REFERENCIA EL PIXEL CENTRAL DE LA MISMA.
  //   EL OUTPUT SIMBOLIZA LA POSICIÓN EN LA FILA DEL PIXEL.
endmodule

module CDN___Chip_desplazamiento_nave (
  input  [3:0] INPUT,
  output _0,
  output _1,
  output _0_2,
  output _1_2,
  output _0_3,
  output _1_3,
  output _0_4,
  output _1_4,
  output _0_5,
  output _1_5,
  output _0_6,
  output _1_6,
  output _0_7,
  output _1_7,
  output _0_8,
  output _1_8,
  output _0_9,
  output _1_9,
  output _0_10,
  output _1_10,
  output _0_11,
  output _1_11,
  output _0_12,
  output _1_12,
  output _0_13,
  output _1_13,
  output _0_14,
  output _1_14,
  output _0_15,
  output _0_16
);

  Decoder #(.select(4)) decoder_1 (
    .out1(_0), .out2(_1_2), .out3(_1_3), .out4(_1_4), .out5(_1_5), .out6(_1_6), .out7(_1_7), .out8(_1_8),
    .out9(_1_9), .out10(_1_10), .out11(_1_11), .out12(_1_12), .out13(_1_13), .out14(_0_16), .sel(INPUT));  // open: out0, out15, en
  or _2 (_0_3, _1_2, _0, _1_3);
  or u__1 (_0_2, _0, _1_2);
  or _3 (_0_4, _1_2, _1_3, _1_4);
  or _4 (_0_5, _1_4, _1_3, _1_5);
  or _5 (_0_6, _1_4, _1_5, _1_6);
  or _6 (_0_7, _1_7, _1_5, _1_6);
  or _7 (_0_8, _1_7, _1_6, _1_8);
  or _8 (_0_9, _1_7, _1_8, _1_9);
  or _10 (_0_11, _1_9, _1_10, _1_11);
  or _9 (_0_10, _1_9, _1_10, _1_8);
  or _11 (_0_12, _1_10, _1_11, _1_12);
  or _12 (_0_13, _1_11, _1_12, _1_13);
  or _14 (_0_15, _1_13, _0_16);
  or _13 (_0_14, _1_12, _1_13, _0_16);

  assign _1 = _0;
  assign _1_14 = _0_16;

  // Notes on the sheet:
  //   OUTPUTS
  //   _sp1_
  //   sp0
  //   _sp2_
  //   _sp3_
  //   EL INPUT ESTÁ PENSADO PARA CONECTARLE LA SALIDA DEL CHIP DE POSICIÓN DE NAVE.
  //   _sp5_
  //   _sp4_
  //   _sp6_
  //   CADA OUTPUT TIENE ARRIBA LA ETIQUETA DE SU SPLITTER CORRESPONDIENTE. EL NÚMERO 0 O 1 INIDCA EL PIN DEL SPLITTER AL CUAL SE DEBE CONECTAR.
  //   _sp7_
  //   _sp8_
  //   _sp9_
  //   _sp10_
  //   _sp11_
  //   _sp12_
  //   _sp13_
  //   _sp14_
  //   sp15
endmodule

module test (
  input  ENTRADA_GATILLO,
  output _2,
  output _3,
  output _4,
  output _5,
  output _6,
  output _7,
  output out_8
);

  wire and_1_out, and_2_out, clock_1_out, nor_1_out, or_1_out;

  Clock clock_1 (.out(clock_1_out));
  and and_1 (and_1_out, ENTRADA_GATILLO, nor_1_out);
  or or_1 (or_1_out, and_1_out, and_2_out);
  and and_2 (and_2_out, clock_1_out, ~nor_1_out);  // AND_Gate
  nor nor_1 (nor_1_out, _2, _3, _4, _5, _6, _7);
  Shift_Register #(.length(6)) shift_register_1 (
    .in(and_1_out), .clk(or_1_out), .q0(_2), .q1(_3), .q2(_4), .q3(_5), .q4(_6), .q5(_7));  // open: shift, out, load, clr, d0, d1, d2, d3, d4, d5
  or or_2 (out_8, _7, _6, _5, _4, _3, _2);

  // Notes on the sheet:
  //   REGISTRO DE LA COLUMNA ACTUAL
  //   FILA 
  //   INDICADOR REGISTRO ACTIVO
  //   SALIDAS DE LED DE (FILA, COLUMNA  ACTUAL)
  //   VAN CONECTADAS A LAS PATAS DEL SPLITTER CORRESPONDIENTE
endmodule

module Nave (
  input  APAGAR,
  input  POWER,
  output out_3
);

  and and_1 (out_3, ~APAGAR, POWER);  // AND_Gate
endmodule

module LEDSWITCH___Power_switch_pantalla_LED (
  input  POWER,
  input  [7:0] in_2,
  input  [7:0] in_3,
  input  [7:0] in_4,
  input  [7:0] in_5,
  input  [7:0] in_6,
  input  [7:0] in_7,
  input  [7:0] in_8,
  input  [7:0] in_9,
  input  [7:0] in_10,
  input  [7:0] in_11,
  input  [7:0] in_12,
  input  [7:0] in_13,
  input  [7:0] in_14,
  input  [7:0] in_15,
  input  [7:0] in_16,
  input  [7:0] in_17,
  output [7:0] out_18,
  output [7:0] out_19,
  output [7:0] out_20,
  output [7:0] out_21,
  output [7:0] out_22,
  output [7:0] out_23,
  output [7:0] out_24,
  output [7:0] out_25,
  output [7:0] out_26,
  output [7:0] out_27,
  output [7:0] out_28,
  output [7:0] out_29,
  output [7:0] out_30,
  output [7:0] out_31,
  output [7:0] out_32,
  output [7:0] out_33
);

  assign out_18 = POWER ? in_2 : 8'bz;  // Controlled_Buffer controlled_buffer_1
  assign out_19 = POWER ? in_3 : 8'bz;  // Controlled_Buffer controlled_buffer_2
  assign out_20 = POWER ? in_4 : 8'bz;  // Controlled_Buffer controlled_buffer_3
  assign out_21 = POWER ? in_5 : 8'bz;  // Controlled_Buffer controlled_buffer_4
  assign out_22 = POWER ? in_6 : 8'bz;  // Controlled_Buffer controlled_buffer_5
  assign out_23 = POWER ? in_7 : 8'bz;  // Controlled_Buffer controlled_buffer_6
  assign out_24 = POWER ? in_8 : 8'bz;  // Controlled_Buffer controlled_buffer_7
  assign out_25 = POWER ? in_9 : 8'bz;  // Controlled_Buffer controlled_buffer_8
  assign out_26 = POWER ? in_10 : 8'bz;  // Controlled_Buffer controlled_buffer_9
  assign out_27 = POWER ? in_11 : 8'bz;  // Controlled_Buffer controlled_buffer_10
  assign out_28 = POWER ? in_12 : 8'bz;  // Controlled_Buffer controlled_buffer_11
  assign out_29 = POWER ? in_13 : 8'bz;  // Controlled_Buffer controlled_buffer_12
  assign out_30 = POWER ? in_14 : 8'bz;  // Controlled_Buffer controlled_buffer_13
  assign out_31 = POWER ? in_15 : 8'bz;  // Controlled_Buffer controlled_buffer_14
  assign out_32 = POWER ? in_16 : 8'bz;  // Controlled_Buffer controlled_buffer_15
  assign out_33 = POWER ? in_17 : 8'bz;  // Controlled_Buffer controlled_buffer_16
endmodule
